// Logisim project Main1_till stage6.circ as structural Verilog: 6 circuits, main circuit main
module main (
);

  wire button_1_out, button_2_out, button_3_out, subcirc_stage1_1_onoff, subcirc_stage2_1_a0,
       subcirc_stage2_1_a1, subcirc_stage2_1_a2, subcirc_stage2_1_a3, subcirc_stage2_1_co,
       subcirc_stage3_1_a0, subcirc_stage3_1_a1, subcirc_stage3_1_a2, subcirc_stage3_1_a3,
       subcirc_stage3_1_co, subcirc_stage4_1_b0, subcirc_stage4_1_b1, subcirc_stage4_1_b2,
       subcirc_stage4_1_b3, subcirc_stage4_1_c0, subcirc_stage4_1_c1, subcirc_stage4_1_c2,
       subcirc_stage4_1_c3;
  wire [3:0] subcirc_stage2_1_out_1, subcirc_stage3_1_o, subcirc_stage4_1_ones, subcirc_stage4_1_tens,
       subcirc_stage6_1_splitout0, subcirc_stage6_1_splitout1, subcirc_stage6_1_splitout2,
       subcirc_stage6_1_splitout3, subcirc_stage6_1_splitout4, subcirc_stage6_2_splitout0,
       subcirc_stage6_2_splitout1, subcirc_stage6_2_splitout2, subcirc_stage6_2_splitout3,
       subcirc_stage6_2_splitout4, subcirc_stage6_3_splitout0, subcirc_stage6_3_splitout1,
       subcirc_stage6_3_splitout2, subcirc_stage6_3_splitout3, subcirc_stage6_3_splitout4,
       subcirc_stage6_4_splitout0, subcirc_stage6_4_splitout1, subcirc_stage6_4_splitout2,
       subcirc_stage6_4_splitout3, subcirc_stage6_4_splitout4;

  Button button_1 (.out(button_1_out));
  LED led_1 (.in(subcirc_stage1_1_onoff));
  Button button_2 (.out(button_2_out));
  Button button_3 (.out(button_3_out));
  Hex_Digit_Display hex_digit_display_1 (.value(subcirc_stage4_1_tens));  // open: dp
  Hex_Digit_Display hex_digit_display_2 (.value(subcirc_stage4_1_ones));  // open: dp
  SubCirc_stage1 subcirc_stage1_1 (.I(button_3_out), .Reset(button_2_out), .Onoff(subcirc_stage1_1_onoff));
  SubCirc_stage2 subcirc_stage2_1 (
    .I(button_3_out), .RESET(button_2_out), .Co(subcirc_stage2_1_co), .out_1(subcirc_stage2_1_out_1),
    .A3(subcirc_stage2_1_a3), .A2(subcirc_stage2_1_a2), .A1(subcirc_stage2_1_a1), .A0(subcirc_stage2_1_a0));
  SubCirc_stage3 subcirc_stage3_1 (
    .CI(subcirc_stage2_1_co), .RESET(button_2_out), .CO(subcirc_stage3_1_co), .O(subcirc_stage3_1_o),
    .A2(subcirc_stage3_1_a2), .A0(subcirc_stage3_1_a0), .A1(subcirc_stage3_1_a1), .A3(subcirc_stage3_1_a3));  // open: in_3
  SubCirc_stage4 subcirc_stage4_1 (
    .Ci(subcirc_stage3_1_co), .RESET(button_2_out), .ONES(subcirc_stage4_1_ones),
    .tens(subcirc_stage4_1_tens), .B3(subcirc_stage4_1_b3), .B2(subcirc_stage4_1_b2),
    .B1(subcirc_stage4_1_b1), .B0(subcirc_stage4_1_b0), .C3(subcirc_stage4_1_c3), .C2(subcirc_stage4_1_c2),
    .C1(subcirc_stage4_1_c1), .C0(subcirc_stage4_1_c0));
  Hex_Digit_Display hex_digit_display_3 (.value(subcirc_stage3_1_o));  // open: dp
  Hex_Digit_Display hex_digit_display_4 (.value(subcirc_stage2_1_out_1));  // open: dp
  Hex_Digit_Display hex_digit_display_5 (.value(subcirc_stage6_3_splitout0));  // open: dp
  Hex_Digit_Display hex_digit_display_6 (.value(subcirc_stage6_4_splitout0));  // open: dp
  SubCirc_stage6 subcirc_stage6_1 (
    .OnOff(subcirc_stage1_1_onoff), .SpliIn(button_1_out), .ResetIn(button_2_out), .i0(subcirc_stage2_1_a0),
    .I1(subcirc_stage2_1_a1), .I2(subcirc_stage2_1_a2), .I3(subcirc_stage2_1_a3),
    .SplitOut0(subcirc_stage6_1_splitout0), .SplitOut2(subcirc_stage6_1_splitout2),
    .SplitOut3(subcirc_stage6_1_splitout3), .SplitOut4(subcirc_stage6_1_splitout4),
    .SplitOut1(subcirc_stage6_1_splitout1));
  SubCirc_stage6 subcirc_stage6_2 (
    .OnOff(subcirc_stage1_1_onoff), .SpliIn(button_1_out), .ResetIn(button_2_out), .i0(subcirc_stage3_1_a0),
    .I1(subcirc_stage3_1_a1), .I2(subcirc_stage3_1_a2), .I3(subcirc_stage3_1_a3),
    .SplitOut0(subcirc_stage6_2_splitout0), .SplitOut2(subcirc_stage6_2_splitout2),
    .SplitOut3(subcirc_stage6_2_splitout3), .SplitOut4(subcirc_stage6_2_splitout4),
    .SplitOut1(subcirc_stage6_2_splitout1));
  Hex_Digit_Display hex_digit_display_7 (.value(subcirc_stage6_1_splitout0));  // open: dp
  Hex_Digit_Display hex_digit_display_8 (.value(subcirc_stage6_2_splitout0));  // open: dp
  SubCirc_stage6 subcirc_stage6_3 (
    .OnOff(subcirc_stage1_1_onoff), .SpliIn(button_1_out), .ResetIn(button_2_out), .i0(subcirc_stage4_1_c0),
    .I1(subcirc_stage4_1_c1), .I2(subcirc_stage4_1_c2), .I3(subcirc_stage4_1_c3),
    .SplitOut0(subcirc_stage6_3_splitout0), .SplitOut2(subcirc_stage6_3_splitout2),
    .SplitOut3(subcirc_stage6_3_splitout3), .SplitOut4(subcirc_stage6_3_splitout4),
    .SplitOut1(subcirc_stage6_3_splitout1));
  SubCirc_stage6 subcirc_stage6_4 (
    .OnOff(subcirc_stage1_1_onoff), .SpliIn(button_1_out), .ResetIn(button_2_out), .i0(subcirc_stage4_1_b0),
    .I1(subcirc_stage4_1_b1), .I2(subcirc_stage4_1_b2), .I3(subcirc_stage4_1_b3),
    .SplitOut0(subcirc_stage6_4_splitout0), .SplitOut2(subcirc_stage6_4_splitout2),
    .SplitOut3(subcirc_stage6_4_splitout3), .SplitOut4(subcirc_stage6_4_splitout4),
    .SplitOut1(subcirc_stage6_4_splitout1));
  Hex_Digit_Display hex_digit_display_9 (.value(subcirc_stage6_3_splitout1));  // open: dp
  Hex_Digit_Display hex_digit_display_10 (.value(subcirc_stage6_3_splitout2));  // open: dp
  Hex_Digit_Display hex_digit_display_11 (.value(subcirc_stage6_3_splitout3));  // open: dp
  Hex_Digit_Display hex_digit_display_12 (.value(subcirc_stage6_3_splitout4));  // open: dp
  Hex_Digit_Display hex_digit_display_13 (.value(subcirc_stage6_4_splitout1));  // open: dp
  Hex_Digit_Display hex_digit_display_14 (.value(subcirc_stage6_2_splitout1));  // open: dp
  Hex_Digit_Display hex_digit_display_15 (.value(subcirc_stage6_4_splitout2));  // open: dp
  Hex_Digit_Display hex_digit_display_16 (.value(subcirc_stage6_4_splitout3));  // open: dp
  Hex_Digit_Display hex_digit_display_17 (.value(subcirc_stage6_4_splitout4));  // open: dp
  Hex_Digit_Display hex_digit_display_18 (.value(subcirc_stage6_1_splitout1));  // open: dp
  Hex_Digit_Display hex_digit_display_19 (.value(subcirc_stage6_2_splitout2));  // open: dp
  Hex_Digit_Display hex_digit_display_20 (.value(subcirc_stage6_1_splitout2));  // open: dp
  Hex_Digit_Display hex_digit_display_21 (.value(subcirc_stage6_2_splitout3));  // open: dp
  Hex_Digit_Display hex_digit_display_22 (.value(subcirc_stage6_1_splitout3));  // open: dp
  Hex_Digit_Display hex_digit_display_23 (.value(subcirc_stage6_2_splitout4));  // open: dp
  Hex_Digit_Display hex_digit_display_24 (.value(subcirc_stage6_1_splitout4));  // open: dp

  // Notes on the sheet:
  //   Split
  //   Clock Started
  //   Reset
  //   Start / Stop
  //   Minutes
  //   Elapsed Time
  //   :
  //   Seconds
  //   Minutes
  //   Stopwatch Interface
  //   Split Time
  //   :
  //   Seconds
  //   :
  //   :
  //   :
  //   :
endmodule

module SubCirc_stage1 (
  input  I,
  input  Reset,
  output Onoff
);

  T_Flip_Flop t_ff_1 (.T(1'b1), .clk(I), .Q(Onoff), .reset(Reset));  // open: Qn, preset
endmodule

module SubCirc_stage2 (
  input  I,
  input  RESET,
  output Co,
  output [3:0] out_1,
  output A3,
  output A2,
  output A1,
  output A0
);

  wire and_1_out, and_2_out, and_3_out, clock_1_out, j_k_ff_1_q, j_k_ff_2_q, j_k_ff_3_q, j_k_ff_4_q,
       or_1_out, t_ff_1_q;

  T_Flip_Flop t_ff_1 (.T(1'b1), .clk(I), .Q(t_ff_1_q), .reset(RESET));  // open: Qn, preset
  Clock clock_1 (.out(clock_1_out));
  and and_1 (and_1_out, t_ff_1_q, clock_1_out);
  J_K_Flip_Flop j_k_ff_1 (
    .J(and_2_out), .K(and_2_out), .clk(and_1_out), .Q(j_k_ff_1_q), .reset(or_1_out));  // open: Qn, preset
  D_Flip_Flop d_ff_1 (.D(j_k_ff_1_q), .clk(and_1_out), .Q(A3), .reset(RESET));  // open: Qn, preset
  and and_2 (and_2_out, j_k_ff_4_q, j_k_ff_3_q, j_k_ff_2_q);
  and and_3 (and_3_out, j_k_ff_4_q, j_k_ff_3_q);
  J_K_Flip_Flop j_k_ff_2 (
    .J(and_3_out), .K(and_3_out), .clk(and_1_out), .Q(j_k_ff_2_q), .reset(or_1_out));  // open: Qn, preset
  D_Flip_Flop d_ff_2 (.D(j_k_ff_2_q), .clk(and_1_out), .Q(A2), .reset(RESET));  // open: Qn, preset
  J_K_Flip_Flop j_k_ff_3 (
    .J(j_k_ff_4_q), .K(j_k_ff_4_q), .clk(and_1_out), .Q(j_k_ff_3_q), .reset(or_1_out));  // open: Qn, preset
  D_Flip_Flop d_ff_3 (.D(j_k_ff_3_q), .clk(and_1_out), .Q(A1), .reset(RESET));  // open: Qn, preset
  J_K_Flip_Flop j_k_ff_4 (.J(1'b1), .K(1'b1), .clk(and_1_out), .Q(j_k_ff_4_q), .reset(or_1_out));  // open: Qn, preset
  D_Flip_Flop d_ff_4 (.D(j_k_ff_4_q), .clk(and_1_out), .Q(A0), .reset(RESET));  // open: Qn, preset
  and and_4 (Co, j_k_ff_1_q, j_k_ff_3_q);
  or or_1 (or_1_out, Co, RESET);

  assign out_1 = {A3, A2, A1, A0};
endmodule

module SubCirc_stage3 (
  input  CI,
  input  RESET,
  input  in_3,
  output CO,
  output [3:0] O,
  output A2,
  output A0,
  output A1,
  output A3
);

  wire and_1_out, clock_1_out, j_k_ff_1_q, j_k_ff_2_q, j_k_ff_3_q, or_1_out;

  J_K_Flip_Flop j_k_ff_1 (
    .J(and_1_out), .K(and_1_out), .clk(CI), .Q(j_k_ff_1_q), .reset(or_1_out));  // open: Qn, preset
  Clock clock_1 (.out(clock_1_out));
  D_Flip_Flop d_ff_1 (.D(j_k_ff_1_q), .clk(clock_1_out), .Q(A2), .reset(RESET));  // open: Qn, preset
  and and_1 (and_1_out, j_k_ff_3_q, j_k_ff_2_q);
  J_K_Flip_Flop j_k_ff_2 (
    .J(j_k_ff_3_q), .K(j_k_ff_3_q), .clk(CI), .Q(j_k_ff_2_q), .reset(or_1_out));  // open: Qn, preset
  D_Flip_Flop d_ff_2 (.D(j_k_ff_2_q), .clk(clock_1_out), .Q(A1), .reset(RESET));  // open: Qn, preset
  J_K_Flip_Flop j_k_ff_3 (.J(1'b1), .K(1'b1), .clk(CI), .Q(j_k_ff_3_q));  // open: Qn, preset, reset
  D_Flip_Flop d_ff_3 (.D(j_k_ff_3_q), .clk(clock_1_out), .Q(A0), .reset(RESET));  // open: Qn, preset
  and and_2 (CO, j_k_ff_1_q, j_k_ff_2_q);
  or or_1 (or_1_out, CO, RESET);

  assign A3 = in_3;
  assign O = {in_3, A2, A1, A0};
endmodule

module SubCirc_stage4 (
  input  Ci,
  input  RESET,
  output [3:0] ONES,
  output [3:0] tens,
  output B3,
  output B2,
  output B1,
  output B0,
  output C3,
  output C2,
  output C1,
  output C0
);

  wire and_1_out, and_2_out, and_3_out, and_4_out, and_5_out, and_6_out, clock_1_out, j_k_ff_1_q, j_k_ff_2_q,
       j_k_ff_3_q, j_k_ff_4_q, j_k_ff_5_q, j_k_ff_6_q, j_k_ff_7_q, j_k_ff_8_q, or_1_out, or_2_out;

  Clock clock_1 (.out(clock_1_out));
  J_K_Flip_Flop j_k_ff_1 (
    .J(and_1_out), .K(and_1_out), .clk(Ci), .Q(j_k_ff_1_q), .reset(or_1_out));  // open: Qn, preset
  D_Flip_Flop d_ff_1 (.D(j_k_ff_1_q), .clk(clock_1_out), .Q(B3), .reset(RESET));  // open: Qn, preset
  and and_1 (and_1_out, j_k_ff_4_q, j_k_ff_3_q, j_k_ff_2_q);
  and and_2 (and_2_out, j_k_ff_4_q, j_k_ff_3_q);
  J_K_Flip_Flop j_k_ff_2 (
    .J(and_2_out), .K(and_2_out), .clk(Ci), .Q(j_k_ff_2_q), .reset(or_1_out));  // open: Qn, preset
  D_Flip_Flop d_ff_2 (.D(j_k_ff_2_q), .clk(clock_1_out), .Q(B2), .reset(RESET));  // open: Qn, preset
  J_K_Flip_Flop j_k_ff_3 (
    .J(j_k_ff_4_q), .K(j_k_ff_4_q), .clk(Ci), .Q(j_k_ff_3_q), .reset(or_1_out));  // open: Qn, preset
  D_Flip_Flop d_ff_3 (.D(j_k_ff_3_q), .clk(clock_1_out), .Q(B1), .reset(RESET));  // open: Qn, preset
  J_K_Flip_Flop j_k_ff_4 (.J(1'b1), .K(1'b1), .clk(Ci), .Q(j_k_ff_4_q), .reset(or_1_out));  // open: Qn, preset
  D_Flip_Flop d_ff_4 (.D(j_k_ff_4_q), .clk(clock_1_out), .Q(B0), .reset(RESET));  // open: Qn, preset
  and and_3 (and_3_out, j_k_ff_1_q, j_k_ff_3_q);
  or or_1 (or_1_out, and_3_out, RESET);
  J_K_Flip_Flop j_k_ff_5 (
    .J(and_4_out), .K(and_4_out), .clk(and_3_out), .Q(j_k_ff_5_q), .reset(or_2_out));  // open: Qn, preset
  D_Flip_Flop d_ff_5 (.D(j_k_ff_5_q), .clk(clock_1_out), .Q(C3), .reset(RESET));  // open: Qn, preset
  and and_4 (and_4_out, j_k_ff_8_q, j_k_ff_7_q, j_k_ff_6_q);
  and and_5 (and_5_out, j_k_ff_8_q, j_k_ff_7_q);
  J_K_Flip_Flop j_k_ff_6 (
    .J(and_5_out), .K(and_5_out), .clk(and_3_out), .Q(j_k_ff_6_q), .reset(or_2_out));  // open: Qn, preset
  D_Flip_Flop d_ff_6 (.D(j_k_ff_6_q), .clk(clock_1_out), .Q(C2), .reset(RESET));  // open: Qn, preset
  J_K_Flip_Flop j_k_ff_7 (
    .J(j_k_ff_8_q), .K(j_k_ff_8_q), .clk(and_3_out), .Q(j_k_ff_7_q), .reset(or_2_out));  // open: Qn, preset
  D_Flip_Flop d_ff_7 (.D(j_k_ff_7_q), .clk(clock_1_out), .Q(C1), .reset(RESET));  // open: Qn, preset
  J_K_Flip_Flop j_k_ff_8 (.J(1'b1), .K(1'b1), .clk(and_3_out), .Q(j_k_ff_8_q), .reset(or_2_out));  // open: Qn, preset
  D_Flip_Flop d_ff_8 (.D(j_k_ff_8_q), .clk(clock_1_out), .Q(C0), .reset(RESET));  // open: Qn, preset
  and and_6 (and_6_out, j_k_ff_5_q, j_k_ff_7_q);
  or or_2 (or_2_out, and_6_out, RESET);

  assign ONES = {B3, B2, B1, B0};
  assign tens = {C3, C2, C1, C0};
endmodule

module SubCirc_stage6 (
  input  OnOff,
  input  SpliIn,
  input  ResetIn,
  input  i0,
  input  I1,
  input  I2,
  input  I3,
  output [3:0] SplitOut0,
  output [3:0] SplitOut2,
  output [3:0] SplitOut3,
  output [3:0] SplitOut4,
  output [3:0] SplitOut1
);

  wire and_1_out, and_2_out, and_3_out, and_4_out, and_5_out, and_6_out, and_7_out, and_8_out, and_9_out,
       and_10_out, and_11_out, and_12_out, and_13_out, and_14_out, and_15_out, and_16_out, and_17_out,
       and_18_out, and_19_out, and_20_out, and_21_out, and_22_out, and_23_out, and_24_out, and_25_out,
       and_26_out, and_27_out, and_28_out, and_29_out, and_30_out, and_31_out, and_32_out, and_33_out,
       and_34_out, and_35_out, and_36_out, and_37_out, and_38_out, and_39_out, and_40_out, and_41_out,
       clock_1_out, d_ff_1_q, d_ff_2_q, d_ff_3_q, d_ff_4_q, d_ff_5_q, d_ff_6_q, d_ff_7_q, d_ff_8_q, d_ff_9_q,
       d_ff_10_q, d_ff_11_q, d_ff_12_q, d_ff_13_q, d_ff_14_q, d_ff_15_q, d_ff_16_q, d_ff_17_q, d_ff_18_q,
       d_ff_19_q, d_ff_20_q, d_ff_21_q, d_ff_22_q, d_ff_23_q, d_ff_24_q, d_ff_25_q, d_ff_26_q, d_ff_27_q,
       d_ff_28_q, d_ff_30_q, d_ff_31_q, d_ff_32_q, d_ff_34_q, d_ff_35_q, d_ff_37_q, d_ff_38_q, d_ff_39_q,
       d_ff_41_q, d_ff_42_q, d_ff_43_q, d_ff_45_q, not_1_out, not_2_out, not_3_out, not_4_out, not_5_out,
       or_1_out, or_2_out, or_3_out, or_4_out, or_5_out, or_6_out, or_7_out, or_8_out, or_9_out, or_10_out,
       or_11_out, or_12_out, or_13_out, or_14_out, or_15_out, or_16_out, or_17_out, or_18_out, or_19_out,
       or_20_out;

  not not_1 (not_1_out, OnOff);
  Clock clock_1 (.out(clock_1_out));
  not not_2 (not_2_out, SpliIn);
  and and_1 (and_1_out, not_2_out, clock_1_out);
  and and_2 (and_2_out, OnOff, i0);
  or or_1 (or_1_out, and_2_out, and_3_out);
  and and_3 (and_3_out, not_1_out, d_ff_3_q);
  D_Flip_Flop d_ff_1 (.D(or_1_out), .clk(SpliIn), .Q(d_ff_1_q), .reset(ResetIn));  // open: Qn, preset
  and and_4 (and_4_out, OnOff, d_ff_1_q);
  D_Flip_Flop d_ff_2 (.D(d_ff_1_q), .clk(and_1_out), .Q(d_ff_2_q), .reset(ResetIn));  // open: Qn, preset
  not not_3 (not_3_out, OnOff);
  not not_4 (not_4_out, OnOff);
  and and_5 (and_5_out, not_1_out, d_ff_8_q);
  or or_2 (or_2_out, and_4_out, and_5_out);
  D_Flip_Flop d_ff_3 (.D(or_2_out), .clk(SpliIn), .Q(d_ff_3_q), .reset(ResetIn));  // open: Qn, preset
  not not_5 (not_5_out, OnOff);
  and and_6 (and_6_out, OnOff, I1);
  or or_3 (or_3_out, and_6_out, and_8_out);
  and and_7 (and_7_out, OnOff, I3);
  or or_4 (or_4_out, and_7_out, and_10_out);
  D_Flip_Flop d_ff_4 (.D(d_ff_3_q), .clk(and_1_out), .Q(d_ff_4_q), .reset(ResetIn));  // open: Qn, preset
  and and_8 (and_8_out, not_3_out, d_ff_13_q);
  D_Flip_Flop d_ff_5 (.D(or_3_out), .clk(SpliIn), .Q(d_ff_5_q), .reset(ResetIn));  // open: Qn, preset
  and and_9 (and_9_out, OnOff, I2);
  and and_10 (and_10_out, not_4_out, d_ff_14_q);
  D_Flip_Flop d_ff_6 (.D(or_4_out), .clk(SpliIn), .Q(d_ff_6_q), .reset(ResetIn));  // open: Qn, preset
  and and_11 (and_11_out, OnOff, d_ff_3_q);
  or or_5 (or_5_out, and_11_out, and_13_out);
  and and_12 (and_12_out, not_5_out, d_ff_15_q);
  or or_6 (or_6_out, and_9_out, and_12_out);
  D_Flip_Flop d_ff_7 (.D(or_6_out), .clk(SpliIn), .Q(d_ff_7_q), .reset(ResetIn));  // open: Qn, preset
  and and_13 (and_13_out, not_1_out, d_ff_16_q);
  D_Flip_Flop d_ff_8 (.D(or_5_out), .clk(SpliIn), .Q(d_ff_8_q), .reset(ResetIn));  // open: Qn, preset
  D_Flip_Flop d_ff_9 (.D(d_ff_5_q), .clk(and_1_out), .Q(d_ff_9_q), .reset(ResetIn));  // open: Qn, preset
  D_Flip_Flop d_ff_10 (.D(d_ff_6_q), .clk(and_1_out), .Q(d_ff_10_q), .reset(ResetIn));  // open: Qn, preset
  and and_14 (and_14_out, OnOff, d_ff_5_q);
  or or_7 (or_7_out, and_14_out, and_16_out);
  D_Flip_Flop d_ff_11 (.D(d_ff_7_q), .clk(and_1_out), .Q(d_ff_11_q), .reset(ResetIn));  // open: Qn, preset
  and and_15 (and_15_out, OnOff, d_ff_6_q);
  or or_8 (or_8_out, and_15_out, and_18_out);
  D_Flip_Flop d_ff_12 (.D(d_ff_8_q), .clk(and_1_out), .Q(d_ff_12_q), .reset(ResetIn));  // open: Qn, preset
  and and_16 (and_16_out, not_3_out, d_ff_21_q);
  D_Flip_Flop d_ff_13 (.D(or_7_out), .clk(SpliIn), .Q(d_ff_13_q), .reset(ResetIn));  // open: Qn, preset
  and and_17 (and_17_out, OnOff, d_ff_7_q);
  or or_9 (or_9_out, and_17_out, and_20_out);
  and and_18 (and_18_out, not_4_out, d_ff_22_q);
  D_Flip_Flop d_ff_14 (.D(or_8_out), .clk(SpliIn), .Q(d_ff_14_q), .reset(ResetIn));  // open: Qn, preset
  and and_19 (and_19_out, OnOff, d_ff_8_q);
  or or_10 (or_10_out, and_19_out, and_21_out);
  and and_20 (and_20_out, not_5_out, d_ff_23_q);
  D_Flip_Flop d_ff_15 (.D(or_9_out), .clk(SpliIn), .Q(d_ff_15_q), .reset(ResetIn));  // open: Qn, preset
  and and_21 (and_21_out, not_1_out, d_ff_24_q);
  D_Flip_Flop d_ff_16 (.D(or_10_out), .clk(SpliIn), .Q(d_ff_16_q), .reset(ResetIn));  // open: Qn, preset
  D_Flip_Flop d_ff_17 (.D(d_ff_13_q), .clk(and_1_out), .Q(d_ff_17_q), .reset(ResetIn));  // open: Qn, preset
  D_Flip_Flop d_ff_18 (.D(d_ff_14_q), .clk(and_1_out), .Q(d_ff_18_q), .reset(ResetIn));  // open: Qn, preset
  and and_22 (and_22_out, OnOff, d_ff_13_q);
  or or_11 (or_11_out, and_22_out, and_24_out);
  D_Flip_Flop d_ff_19 (.D(d_ff_15_q), .clk(and_1_out), .Q(d_ff_19_q), .reset(ResetIn));  // open: Qn, preset
  and and_23 (and_23_out, OnOff, d_ff_14_q);
  or or_12 (or_12_out, and_23_out, and_26_out);
  D_Flip_Flop d_ff_20 (.D(d_ff_16_q), .clk(and_1_out), .Q(d_ff_20_q), .reset(ResetIn));  // open: Qn, preset
  and and_24 (and_24_out, not_3_out, d_ff_30_q);
  D_Flip_Flop d_ff_21 (.D(or_11_out), .clk(SpliIn), .Q(d_ff_21_q), .reset(ResetIn));  // open: Qn, preset
  and and_25 (and_25_out, OnOff, d_ff_15_q);
  and and_26 (and_26_out, not_4_out, d_ff_31_q);
  D_Flip_Flop d_ff_22 (.D(or_12_out), .clk(SpliIn), .Q(d_ff_22_q), .reset(ResetIn));  // open: Qn, preset
  and and_27 (and_27_out, OnOff, d_ff_16_q);
  or or_13 (or_13_out, and_27_out, and_29_out);
  and and_28 (and_28_out, not_5_out, d_ff_32_q);
  or or_14 (or_14_out, and_25_out, and_28_out);
  D_Flip_Flop d_ff_23 (.D(or_14_out), .clk(SpliIn), .Q(d_ff_23_q), .reset(ResetIn));  // open: Qn, preset
  and and_29 (and_29_out, not_1_out, SplitOut0[0]);
  D_Flip_Flop d_ff_24 (.D(or_13_out), .clk(SpliIn), .Q(d_ff_24_q), .reset(ResetIn));  // open: Qn, preset
  D_Flip_Flop d_ff_25 (.D(d_ff_21_q), .clk(and_1_out), .Q(d_ff_25_q), .reset(ResetIn));  // open: Qn, preset
  D_Flip_Flop d_ff_26 (.D(d_ff_22_q), .clk(and_1_out), .Q(d_ff_26_q), .reset(ResetIn));  // open: Qn, preset
  D_Flip_Flop d_ff_27 (.D(d_ff_24_q), .clk(and_1_out), .Q(d_ff_27_q), .reset(ResetIn));  // open: Qn, preset
  and and_30 (and_30_out, OnOff, d_ff_21_q);
  or or_15 (or_15_out, and_30_out, and_32_out);
  D_Flip_Flop d_ff_28 (.D(d_ff_23_q), .clk(and_1_out), .Q(d_ff_28_q), .reset(ResetIn));  // open: Qn, preset
  and and_31 (and_31_out, OnOff, d_ff_22_q);
  or or_16 (or_16_out, and_31_out, and_34_out);
  D_Flip_Flop d_ff_29 (.D(d_ff_2_q), .clk(and_1_out), .Q(SplitOut0[0]), .reset(ResetIn));  // open: Qn, preset
  and and_32 (and_32_out, not_3_out, d_ff_38_q);
  D_Flip_Flop d_ff_30 (.D(or_15_out), .clk(SpliIn), .Q(d_ff_30_q), .reset(ResetIn));  // open: Qn, preset
  and and_33 (and_33_out, OnOff, d_ff_23_q);
  and and_34 (and_34_out, not_4_out, d_ff_39_q);
  D_Flip_Flop d_ff_31 (.D(or_16_out), .clk(SpliIn), .Q(d_ff_31_q), .reset(ResetIn));  // open: Qn, preset
  and and_35 (and_35_out, not_5_out, d_ff_42_q);
  or or_17 (or_17_out, and_33_out, and_35_out);
  D_Flip_Flop d_ff_32 (.D(or_17_out), .clk(SpliIn), .Q(d_ff_32_q), .reset(ResetIn));  // open: Qn, preset
  D_Flip_Flop d_ff_33 (.D(d_ff_4_q), .clk(and_1_out), .Q(SplitOut1[0]), .reset(ResetIn));  // open: Qn, preset
  D_Flip_Flop d_ff_34 (.D(d_ff_30_q), .clk(and_1_out), .Q(d_ff_34_q), .reset(ResetIn));  // open: Qn, preset
  D_Flip_Flop d_ff_35 (.D(d_ff_31_q), .clk(and_1_out), .Q(d_ff_35_q), .reset(ResetIn));  // open: Qn, preset
  D_Flip_Flop d_ff_36 (.D(d_ff_12_q), .clk(and_1_out), .Q(SplitOut2[0]), .reset(ResetIn));  // open: Qn, preset
  and and_36 (and_36_out, OnOff, d_ff_30_q);
  or or_18 (or_18_out, and_36_out, and_38_out);
  D_Flip_Flop d_ff_37 (.D(d_ff_32_q), .clk(and_1_out), .Q(d_ff_37_q), .reset(ResetIn));  // open: Qn, preset
  and and_37 (and_37_out, OnOff, d_ff_31_q);
  or or_19 (or_19_out, and_37_out, and_40_out);
  and and_38 (and_38_out, not_3_out, SplitOut0[1]);
  D_Flip_Flop d_ff_38 (.D(or_18_out), .clk(SpliIn), .Q(d_ff_38_q), .reset(ResetIn));  // open: Qn, preset
  and and_39 (and_39_out, OnOff, d_ff_32_q);
  and and_40 (and_40_out, not_4_out, SplitOut0[3]);
  D_Flip_Flop d_ff_39 (.D(or_19_out), .clk(SpliIn), .Q(d_ff_39_q), .reset(ResetIn));  // open: Qn, preset
  D_Flip_Flop d_ff_40 (.D(d_ff_20_q), .clk(and_1_out), .Q(SplitOut3[0]), .reset(ResetIn));  // open: Qn, preset
  D_Flip_Flop d_ff_41 (.D(d_ff_38_q), .clk(and_1_out), .Q(d_ff_41_q), .reset(ResetIn));  // open: Qn, preset
  and and_41 (and_41_out, not_5_out, SplitOut0[2]);
  or or_20 (or_20_out, and_39_out, and_41_out);
  D_Flip_Flop d_ff_42 (.D(or_20_out), .clk(SpliIn), .Q(d_ff_42_q), .reset(ResetIn));  // open: Qn, preset
  D_Flip_Flop d_ff_43 (.D(d_ff_39_q), .clk(and_1_out), .Q(d_ff_43_q), .reset(ResetIn));  // open: Qn, preset
  D_Flip_Flop d_ff_44 (.D(d_ff_9_q), .clk(and_1_out), .Q(SplitOut0[1]), .reset(ResetIn));  // open: Qn, preset
  D_Flip_Flop d_ff_45 (.D(d_ff_42_q), .clk(and_1_out), .Q(d_ff_45_q), .reset(ResetIn));  // open: Qn, preset
  D_Flip_Flop d_ff_46 (.D(d_ff_10_q), .clk(and_1_out), .Q(SplitOut0[3]), .reset(ResetIn));  // open: Qn, preset
  D_Flip_Flop d_ff_47 (.D(d_ff_27_q), .clk(and_1_out), .Q(SplitOut4[0]), .reset(ResetIn));  // open: Qn, preset
  D_Flip_Flop d_ff_48 (.D(d_ff_17_q), .clk(and_1_out), .Q(SplitOut1[1]), .reset(ResetIn));  // open: Qn, preset
  D_Flip_Flop d_ff_49 (.D(d_ff_11_q), .clk(and_1_out), .Q(SplitOut0[2]), .reset(ResetIn));  // open: Qn, preset
  D_Flip_Flop d_ff_50 (.D(d_ff_18_q), .clk(and_1_out), .Q(SplitOut1[3]), .reset(ResetIn));  // open: Qn, preset
  D_Flip_Flop d_ff_51 (.D(d_ff_25_q), .clk(and_1_out), .Q(SplitOut2[1]), .reset(ResetIn));  // open: Qn, preset
  D_Flip_Flop d_ff_52 (.D(d_ff_19_q), .clk(and_1_out), .Q(SplitOut1[2]), .reset(ResetIn));  // open: Qn, preset
  D_Flip_Flop d_ff_53 (.D(d_ff_26_q), .clk(and_1_out), .Q(SplitOut2[3]), .reset(ResetIn));  // open: Qn, preset
  D_Flip_Flop d_ff_54 (.D(d_ff_34_q), .clk(and_1_out), .Q(SplitOut3[1]), .reset(ResetIn));  // open: Qn, preset
  D_Flip_Flop d_ff_55 (.D(d_ff_28_q), .clk(and_1_out), .Q(SplitOut2[2]), .reset(ResetIn));  // open: Qn, preset
  D_Flip_Flop d_ff_56 (.D(d_ff_35_q), .clk(and_1_out), .Q(SplitOut3[3]), .reset(ResetIn));  // open: Qn, preset
  D_Flip_Flop d_ff_57 (.D(d_ff_37_q), .clk(and_1_out), .Q(SplitOut3[2]), .reset(ResetIn));  // open: Qn, preset
  D_Flip_Flop d_ff_58 (.D(d_ff_41_q), .clk(and_1_out), .Q(SplitOut4[1]), .reset(ResetIn));  // open: Qn, preset
  D_Flip_Flop d_ff_59 (.D(d_ff_43_q), .clk(and_1_out), .Q(SplitOut4[3]), .reset(ResetIn));  // open: Qn, preset
  D_Flip_Flop d_ff_60 (.D(d_ff_45_q), .clk(and_1_out), .Q(SplitOut4[2]), .reset(ResetIn));  // open: Qn, preset
endmodule
