// Logisim project Stage1.circ as structural Verilog: 1 circuit, main circuit main
module main (
);

  wire button_1_out, t_ff_1_q;

  Button button_1 (.out(button_1_out));
  T_Flip_Flop t_ff_1 (.T(1'b1), .clk(button_1_out), .Q(t_ff_1_q));  // open: Qn, reset, preset
  LED led_1 (.in(t_ff_1_q));

  // Notes on the sheet:
  //   start/stop
  //   Stage 1
  //   T Flip-flop
  //   output
endmodule
