// Logisim project main2_till stage5.circ as structural Verilog: 1 circuit, main circuit main
module main (
  input  in_1,
  input  in_2
);

  wire and_1_out, and_2_out, and_3_out, and_4_out, and_5_out, and_6_out, and_7_out, and_8_out, and_9_out,
       and_10_out, and_11_out, and_12_out, and_13_out, button_1_out, button_2_out, button_3_out, clock_1_out,
       j_k_ff_1_q, j_k_ff_2_q, j_k_ff_3_q, j_k_ff_4_q, j_k_ff_5_q, j_k_ff_6_q, j_k_ff_7_q, j_k_ff_8_q,
       j_k_ff_9_q, j_k_ff_10_q, j_k_ff_11_q, j_k_ff_12_q, j_k_ff_13_q, j_k_ff_14_q, j_k_ff_15_q, or_1_out,
       or_2_out, or_3_out, or_4_out, t_ff_1_q;
  wire [2:0] d_ff_4_q, d_ff_17_q;
  wire [3:0] d_ff_1_q, d_ff_2_q, d_ff_3_q, d_ff_16_q, d_ff_18_q, d_ff_19_q;

  Hex_Digit_Display hex_digit_display_1 (.value(d_ff_19_q));  // open: dp
  Hex_Digit_Display hex_digit_display_2 (.value(d_ff_18_q));  // open: dp
  Button button_1 (.out(button_1_out));
  Hex_Digit_Display hex_digit_display_3 (.value({in_2, d_ff_17_q}));  // open: dp
  Hex_Digit_Display hex_digit_display_4 (.value(d_ff_16_q));  // open: dp
  Button button_2 (.out(button_2_out));
  Hex_Digit_Display hex_digit_display_5 (.value(d_ff_2_q));  // open: dp
  Hex_Digit_Display hex_digit_display_6 (.value(d_ff_1_q));  // open: dp
  Button button_3 (.out(button_3_out));
  Hex_Digit_Display hex_digit_display_7 (.value({in_1, d_ff_4_q}));  // open: dp
  Hex_Digit_Display hex_digit_display_8 (.value(d_ff_3_q));  // open: dp
  Clock clock_1 (.out(clock_1_out));
  T_Flip_Flop t_ff_1 (.T(1'b1), .clk(button_3_out), .Q(t_ff_1_q), .reset(button_1_out));  // open: Qn, preset
  J_K_Flip_Flop j_k_ff_1 (.J(1'b1), .K(1'b1), .clk(or_1_out), .Q(j_k_ff_1_q), .reset(or_2_out));  // open: Qn, preset
  J_K_Flip_Flop j_k_ff_2 (.J(1'b1), .K(1'b1), .clk(or_2_out), .Q(j_k_ff_2_q), .reset(or_3_out));  // open: Qn, preset
  J_K_Flip_Flop j_k_ff_3 (.J(1'b1), .K(1'b1), .clk(or_3_out), .Q(j_k_ff_3_q), .reset(or_4_out));  // open: Qn, preset
  LED led_1 (.in(t_ff_1_q));
  J_K_Flip_Flop j_k_ff_4 (
    .J(t_ff_1_q), .K(t_ff_1_q), .clk(clock_1_out), .Q(j_k_ff_4_q), .reset(or_1_out));  // open: Qn, preset
  D_Flip_Flop d_ff_1 (.D(j_k_ff_2_q), .clk(clock_1_out), .Q(d_ff_1_q[0]), .reset(button_1_out));  // open: Qn, preset
  D_Flip_Flop d_ff_2 (.D(j_k_ff_3_q), .clk(clock_1_out), .Q(d_ff_2_q[0]), .reset(button_1_out));  // open: Qn, preset
  and and_1 (and_1_out, t_ff_1_q, j_k_ff_4_q);
  D_Flip_Flop d_ff_3 (.D(j_k_ff_4_q), .clk(clock_1_out), .Q(d_ff_3_q[0]), .reset(button_1_out));  // open: Qn, preset
  J_K_Flip_Flop j_k_ff_5 (
    .J(j_k_ff_1_q), .K(j_k_ff_1_q), .clk(or_1_out), .Q(j_k_ff_5_q), .reset(or_2_out));  // open: Qn, preset
  D_Flip_Flop d_ff_4 (.D(j_k_ff_1_q), .clk(clock_1_out), .Q(d_ff_4_q[0]), .reset(button_1_out));  // open: Qn, preset
  J_K_Flip_Flop j_k_ff_6 (
    .J(j_k_ff_2_q), .K(j_k_ff_2_q), .clk(or_2_out), .Q(j_k_ff_6_q), .reset(or_3_out));  // open: Qn, preset
  J_K_Flip_Flop j_k_ff_7 (
    .J(j_k_ff_3_q), .K(j_k_ff_3_q), .clk(or_3_out), .Q(j_k_ff_7_q), .reset(or_4_out));  // open: Qn, preset
  J_K_Flip_Flop j_k_ff_8 (
    .J(and_1_out), .K(and_1_out), .clk(clock_1_out), .Q(j_k_ff_8_q), .reset(or_1_out));  // open: Qn, preset
  D_Flip_Flop d_ff_5 (.D(j_k_ff_6_q), .clk(clock_1_out), .Q(d_ff_1_q[1]), .reset(button_1_out));  // open: Qn, preset
  D_Flip_Flop d_ff_6 (.D(j_k_ff_7_q), .clk(clock_1_out), .Q(d_ff_2_q[1]), .reset(button_1_out));  // open: Qn, preset
  and and_2 (and_2_out, and_1_out, j_k_ff_8_q);
  D_Flip_Flop d_ff_7 (.D(j_k_ff_8_q), .clk(clock_1_out), .Q(d_ff_3_q[1]), .reset(button_1_out));  // open: Qn, preset
  and and_3 (and_3_out, j_k_ff_1_q, j_k_ff_5_q);
  D_Flip_Flop d_ff_8 (.D(j_k_ff_5_q), .clk(clock_1_out), .Q(d_ff_4_q[1]), .reset(button_1_out));  // open: Qn, preset
  and and_4 (and_4_out, j_k_ff_2_q, j_k_ff_6_q);
  J_K_Flip_Flop j_k_ff_9 (
    .J(and_4_out), .K(and_4_out), .clk(or_2_out), .Q(j_k_ff_9_q), .reset(or_3_out));  // open: Qn, preset
  and and_5 (and_5_out, j_k_ff_3_q, j_k_ff_7_q);
  J_K_Flip_Flop j_k_ff_10 (
    .J(and_5_out), .K(and_5_out), .clk(or_3_out), .Q(j_k_ff_10_q), .reset(or_4_out));  // open: Qn, preset
  J_K_Flip_Flop j_k_ff_11 (
    .J(and_2_out), .K(and_2_out), .clk(clock_1_out), .Q(j_k_ff_11_q), .reset(or_1_out));  // open: Qn, preset
  J_K_Flip_Flop j_k_ff_12 (
    .J(and_3_out), .K(and_3_out), .clk(or_1_out), .Q(j_k_ff_12_q), .reset(or_2_out));  // open: Qn, preset
  D_Flip_Flop d_ff_9 (.D(j_k_ff_9_q), .clk(clock_1_out), .Q(d_ff_1_q[2]), .reset(button_1_out));  // open: Qn, preset
  D_Flip_Flop d_ff_10 (.D(j_k_ff_10_q), .clk(clock_1_out), .Q(d_ff_2_q[2]), .reset(button_1_out));  // open: Qn, preset
  D_Flip_Flop d_ff_11 (.D(j_k_ff_11_q), .clk(clock_1_out), .Q(d_ff_3_q[2]), .reset(button_1_out));  // open: Qn, preset
  and and_6 (and_6_out, and_4_out, j_k_ff_9_q);
  and and_7 (and_7_out, and_5_out, j_k_ff_10_q);
  J_K_Flip_Flop j_k_ff_13 (
    .J(and_7_out), .K(and_7_out), .clk(or_3_out), .Q(j_k_ff_13_q), .reset(or_4_out));  // open: Qn, preset
  and and_8 (and_8_out, and_2_out, j_k_ff_11_q);
  J_K_Flip_Flop j_k_ff_14 (
    .J(and_8_out), .K(and_8_out), .clk(clock_1_out), .Q(j_k_ff_14_q), .reset(or_1_out));  // open: Qn, preset
  and and_9 (and_9_out, j_k_ff_5_q, j_k_ff_12_q);
  D_Flip_Flop d_ff_12 (.D(j_k_ff_12_q), .clk(clock_1_out), .Q(d_ff_4_q[2]), .reset(button_1_out));  // open: Qn, preset
  J_K_Flip_Flop j_k_ff_15 (
    .J(and_6_out), .K(and_6_out), .clk(or_2_out), .Q(j_k_ff_15_q), .reset(or_3_out));  // open: Qn, preset
  D_Flip_Flop d_ff_13 (.D(j_k_ff_14_q), .clk(clock_1_out), .Q(d_ff_3_q[3]), .reset(button_1_out));  // open: Qn, preset
  and and_10 (and_10_out, j_k_ff_6_q, j_k_ff_15_q);
  D_Flip_Flop d_ff_14 (.D(j_k_ff_15_q), .clk(clock_1_out), .Q(d_ff_1_q[3]), .reset(button_1_out));  // open: Qn, preset
  and and_11 (and_11_out, j_k_ff_7_q, j_k_ff_13_q);
  D_Flip_Flop d_ff_15 (.D(j_k_ff_13_q), .clk(clock_1_out), .Q(d_ff_2_q[3]), .reset(button_1_out));  // open: Qn, preset
  and and_12 (and_12_out, j_k_ff_8_q, j_k_ff_14_q);
  or or_1 (or_1_out, and_12_out, button_1_out);
  or or_2 (or_2_out, and_9_out, button_1_out);
  or or_3 (or_3_out, and_10_out, button_1_out);
  or or_4 (or_4_out, and_11_out, button_1_out);
  and and_13 (and_13_out, t_ff_1_q, button_2_out);
  D_Flip_Flop d_ff_16 (.D(d_ff_3_q[0]), .clk(and_13_out), .Q(d_ff_16_q[0]), .reset(button_1_out));  // open: Qn, preset
  D_Flip_Flop d_ff_17 (.D(d_ff_4_q[0]), .clk(and_13_out), .Q(d_ff_17_q[0]), .reset(button_1_out));  // open: Qn, preset
  D_Flip_Flop d_ff_18 (.D(d_ff_1_q[0]), .clk(and_13_out), .Q(d_ff_18_q[0]), .reset(button_1_out));  // open: Qn, preset
  D_Flip_Flop d_ff_19 (.D(d_ff_2_q[0]), .clk(and_13_out), .Q(d_ff_19_q[0]), .reset(button_1_out));  // open: Qn, preset
  D_Flip_Flop d_ff_20 (.D(d_ff_3_q[1]), .clk(and_13_out), .Q(d_ff_16_q[1]), .reset(button_1_out));  // open: Qn, preset
  D_Flip_Flop d_ff_21 (.D(d_ff_4_q[1]), .clk(and_13_out), .Q(d_ff_17_q[1]), .reset(button_1_out));  // open: Qn, preset
  D_Flip_Flop d_ff_22 (.D(d_ff_1_q[1]), .clk(and_13_out), .Q(d_ff_18_q[1]), .reset(button_1_out));  // open: Qn, preset
  D_Flip_Flop d_ff_23 (.D(d_ff_2_q[1]), .clk(and_13_out), .Q(d_ff_19_q[1]), .reset(button_1_out));  // open: Qn, preset
  D_Flip_Flop d_ff_24 (.D(d_ff_3_q[2]), .clk(and_13_out), .Q(d_ff_16_q[2]), .reset(button_1_out));  // open: Qn, preset
  D_Flip_Flop d_ff_25 (.D(d_ff_4_q[2]), .clk(and_13_out), .Q(d_ff_17_q[2]), .reset(button_1_out));  // open: Qn, preset
  D_Flip_Flop d_ff_26 (.D(d_ff_1_q[2]), .clk(and_13_out), .Q(d_ff_18_q[2]), .reset(button_1_out));  // open: Qn, preset
  D_Flip_Flop d_ff_27 (.D(d_ff_2_q[2]), .clk(and_13_out), .Q(d_ff_19_q[2]), .reset(button_1_out));  // open: Qn, preset
  D_Flip_Flop d_ff_28 (.D(d_ff_3_q[3]), .clk(and_13_out), .Q(d_ff_16_q[3]), .reset(button_1_out));  // open: Qn, preset
  D_Flip_Flop d_ff_29 (.D(d_ff_1_q[3]), .clk(and_13_out), .Q(d_ff_18_q[3]), .reset(button_1_out));  // open: Qn, preset
  D_Flip_Flop d_ff_30 (.D(d_ff_2_q[3]), .clk(and_13_out), .Q(d_ff_19_q[3]), .reset(button_1_out));  // open: Qn, preset

  // Notes on the sheet:
  //   Minutes
  //   Reset
  //   Split Time
  //   :
  //   Seconds
  //   Split
  //   Minutes
  //   Elapsed Time
  //   :
  //   Start / Stop
  //   Seconds
  //   clock
  //   Clock Started
  //   STOPWATCH  INTERFACE
  //   STAGE 5
endmodule
