// Logisim project stage2.circ as structural Verilog: 1 circuit, main circuit main
module main (
);

  wire and_1_out, and_2_out, and_3_out, and_4_out, button_1_out, button_3_out, clock_1_out, j_k_ff_1_q,
       j_k_ff_2_q, j_k_ff_3_q, j_k_ff_4_q, or_1_out, t_ff_1_q;
  wire [3:0] d_ff_1_q;

  Hex_Digit_Display hex_digit_display_1 ();  // open: value, dp
  Button button_1 (.out(button_1_out));
  Hex_Digit_Display hex_digit_display_2 ();  // open: value, dp
  Hex_Digit_Display hex_digit_display_3 ();  // open: value, dp
  Hex_Digit_Display hex_digit_display_4 ();  // open: value, dp
  Button button_2 ();  // open: out
  Hex_Digit_Display hex_digit_display_5 ();  // open: value, dp
  Hex_Digit_Display hex_digit_display_6 ();  // open: value, dp
  Button button_3 (.out(button_3_out));
  Hex_Digit_Display hex_digit_display_7 ();  // open: value, dp
  Hex_Digit_Display hex_digit_display_8 (.value(d_ff_1_q));  // open: dp
  LED led_1 (.in(t_ff_1_q));
  T_Flip_Flop t_ff_1 (.T(1'b1), .clk(button_3_out), .Q(t_ff_1_q), .reset(button_1_out));  // open: Qn, preset
  J_K_Flip_Flop j_k_ff_1 (
    .J(t_ff_1_q), .K(t_ff_1_q), .clk(clock_1_out), .Q(j_k_ff_1_q), .reset(or_1_out));  // open: Qn, preset
  and and_1 (and_1_out, t_ff_1_q, j_k_ff_1_q);
  D_Flip_Flop d_ff_1 (.D(j_k_ff_1_q), .clk(clock_1_out), .Q(d_ff_1_q[0]), .reset(button_1_out));  // open: Qn, preset
  J_K_Flip_Flop j_k_ff_2 (
    .J(and_1_out), .K(and_1_out), .clk(clock_1_out), .Q(j_k_ff_2_q), .reset(or_1_out));  // open: Qn, preset
  and and_2 (and_2_out, and_1_out, j_k_ff_2_q);
  D_Flip_Flop d_ff_2 (.D(j_k_ff_2_q), .clk(clock_1_out), .Q(d_ff_1_q[1]), .reset(button_1_out));  // open: Qn, preset
  J_K_Flip_Flop j_k_ff_3 (
    .J(and_2_out), .K(and_2_out), .clk(clock_1_out), .Q(j_k_ff_3_q), .reset(or_1_out));  // open: Qn, preset
  D_Flip_Flop d_ff_3 (.D(j_k_ff_3_q), .clk(clock_1_out), .Q(d_ff_1_q[2]), .reset(button_1_out));  // open: Qn, preset
  Clock clock_1 (.out(clock_1_out));
  and and_3 (and_3_out, and_2_out, j_k_ff_3_q);
  J_K_Flip_Flop j_k_ff_4 (
    .J(and_3_out), .K(and_3_out), .clk(clock_1_out), .Q(j_k_ff_4_q), .reset(or_1_out));  // open: Qn, preset
  D_Flip_Flop d_ff_4 (.D(j_k_ff_4_q), .clk(clock_1_out), .Q(d_ff_1_q[3]), .reset(button_1_out));  // open: Qn, preset
  and and_4 (and_4_out, j_k_ff_2_q, j_k_ff_4_q);
  or or_1 (or_1_out, and_4_out, button_1_out);

  // Notes on the sheet:
  //   Minutes
  //   Reset
  //   Split Time
  //   :
  //   Seconds
  //   Split
  //   Minutes
  //   Elapsed Time
  //   :
  //   Start / Stop
  //   Seconds
  //   Clock Started
  //   Stopwatch Interface
  //   Clock
endmodule
